# Fritzing sketch tag-bag (saved by Fritzing 0.9.3b)
breadboards: 1

parts:
  NodeMCU_ESP8266_Microcontroller = NodeMCU V3.0
  RC522_(RFID_Reader) = RFID-RC522-v2
  Fan_1_(temperature_based) = Fan - Ventilador [package=THT]
  Fan_2_(for_NodeMCU) = Fan - Ventilador [package=THT]
  R1 = Resistor [tolerance=±5% resistance=220 package=THT]
  Force_Sensing_Resistor = Basic Force Sensing Resistor (FSR) [package=THT]
  LM35_(Temperature_Sensor) = LM35 Temperature Sensor [package="TO92 [THT]"]
  LED = LED - 3mm [color="Green (565nm)" package="3 mm [THT]"]

nets:
  N1: NodeMCU_ESP8266_Microcontroller.D0, RC522_(RFID_Reader).RST
  N2: NodeMCU_ESP8266_Microcontroller.D1, Fan_1_(temperature_based).5V
  N3: NodeMCU_ESP8266_Microcontroller.D2, R1.Pin_0, Force_Sensing_Resistor.pin_1
  3V3: NodeMCU_ESP8266_Microcontroller.3V3, RC522_(RFID_Reader).3.3V, Fan_2_(for_NodeMCU).5V, Force_Sensing_Resistor.pin_0
  GND: NodeMCU_ESP8266_Microcontroller.GND#6, NodeMCU_ESP8266_Microcontroller.GND#13, NodeMCU_ESP8266_Microcontroller.GND#16, NodeMCU_ESP8266_Microcontroller.GND#33, RC522_(RFID_Reader).GND, Fan_1_(temperature_based).GND, Fan_2_(for_NodeMCU).GND, R1.Pin_1, LM35_(Temperature_Sensor).GND, LED.cathode
  N4: NodeMCU_ESP8266_Microcontroller.D5, RC522_(RFID_Reader).SCK
  N5: NodeMCU_ESP8266_Microcontroller.D6, RC522_(RFID_Reader).MISO
  N6: NodeMCU_ESP8266_Microcontroller.D7, RC522_(RFID_Reader).MOSI
  N7: NodeMCU_ESP8266_Microcontroller.D8, RC522_(RFID_Reader).SDA
  N8: NodeMCU_ESP8266_Microcontroller.Vin, LM35_(Temperature_Sensor).+Vs
  N9: NodeMCU_ESP8266_Microcontroller.A0, LM35_(Temperature_Sensor).Vout

custom parts:
  NodeMCU V3.0: ESP8266 based NodeMCU
  RFID-RC522-v2: A simple China made RFID-RC522 Reader; do check the pin labels, as this is a MFRC522 based clone.
  Fan - Ventilador: Ventilador de 2 pines, se encuentra comunmente en computadoras de escritorio
